# Fritzing sketch lightcon4 (saved by Fritzing 0.9.3b)
circuit board: 5.87768cm x 7.77243cm
breadboards: 1

parts:
  M1 = DOIT Esp32 DevKit v1 (30 pins long, 11 pins width) [part_number=ESP32S-PIN30]
  R03 = Resistor [tolerance=±5% resistance=680 package=THT]
  VOUT03 = Power Jack [package=power_jack_slot]
  VIN = Power Jack [package=power_jack_slot]
  VOUT01 = Power Jack [package=power_jack_slot]
  Q03 = TIP120 Hi-Current Darlington Transistor
  Q01 = TIP120 Hi-Current Darlington Transistor
  R01 = Resistor [tolerance=±5% resistance=680 package=THT]
  Q04 = TIP120 Hi-Current Darlington Transistor
  R04 = Resistor [tolerance=±5% resistance=680 package=THT]
  VOUT04 = Power Jack [package=power_jack_slot]
  Q13 = TIP120 Hi-Current Darlington Transistor
  R13 = Resistor [tolerance=±5% resistance=680 package=THT]
  VOUT13 = Power Jack [package=power_jack_slot]
  R0 = Resistor [tolerance=±5% resistance=220 package=THT]
  LED = LED - 5mm [color="Red (633nm)" package="5 mm [THT]"]

nets:
  GND: M1.GND, VIN.GND, Q03.EMITTER, Q01.EMITTER, Q04.EMITTER, Q13.EMITTER, LED.cathode
  N1: M1.D2, R0.Pin_0
  N2: M1.D4, R04.Pin_0
  N3: M1.RX0, R03.Pin_0
  N4: M1.TX0, R01.Pin_0
  N5: M1.D13, R13.Pin_0
  N6: M1.VIN, VOUT03.PWR, VIN.PWR, VOUT01.PWR, VOUT04.PWR, VOUT13.PWR
  N7: R03.Pin_1, Q03.BASE
  N8: VOUT03.GND, Q03.COLLECTOR
  N9: VOUT01.GND, Q01.COLLECTOR
  N10: Q01.BASE, R01.Pin_1
  N11: Q04.BASE, R04.Pin_1
  N12: Q04.COLLECTOR, VOUT04.GND
  N13: Q13.BASE, R13.Pin_1
  N14: Q13.COLLECTOR, VOUT13.GND
  N15: R0.Pin_1, LED.anode

notes:
  lightcon4
  4 channel light controller
  Knowit Hardware Guild
  ESP32 Devkit
  Voltage input/ output: 5V - 12V
  201901
  Not to be used with motors!

custom parts:
  DOIT Esp32 DevKit v1 (30 pins long, 11 pins width): The DOIT Esp32 DevKit v1 is one of the development board created by DOIT to evaluate the ESP-WROOM-32 module. It is based on the ESP32 microcontroller that boasts Wifi, Bluetooth, Ethernet and Low Power support all in a single chip. (vanepp) made breadboard work, adjusted pin numbering and labels and reduced size of schematic and cleaned up pcb. This chip is 30pins long (2 x15) and 11 pins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
